// Logisim project alu.circ as structural Verilog: 20 circuits, main circuit main
module main (
  input  [7:0] in_1,
  input  [7:0] in_2,
  input  [2:0] in_3,
  output [7:0] Output,
  output Unsigned_Overflow,
  output Signed_Overflow,
  output [7:0] out_7,
  output [7:0] Output_2,
  output Unsigned_Overflow_2,
  output Signed_Overflow_2,
  output [7:0] out_11,
  output [7:0] Output_3,
  output Unsigned_Overflow_3,
  output Signed_Overflow_3,
  output [7:0] out_15,
  output [7:0] Output_4,
  output Unsigned_Overflow_4,
  output Signed_Overflow_4,
  output [7:0] out_19,
  output [7:0] Output_5,
  output Unsigned_Overflow_5,
  output Signed_Overflow_5,
  output [7:0] out_23,
  output [7:0] Output_6,
  output Unsigned_Overflow_6,
  output Signed_Overflow_6,
  output [7:0] SIGNED_LESS_THAN,
  output [7:0] out_28,
  output [7:0] Output_7,
  output Unsigned_Overflow_7,
  output Signed_Overflow_7,
  output [7:0] out_32,
  output [7:0] Output_8,
  output Unsigned_Overflow_8,
  output Signed_Overflow_8,
  output [7:0] out_36,
  output [7:0] Output_9,
  output Unsigned_Overflow_9,
  output Signed_Overflow_9
);

  wire clock_1_out;

  Clock #(.highDuration(1), .lowDuration(1)) clock_1 (.out(clock_1_out));
  _1_to_256_Iterator u_1_to_256_iterator_1 (.Clock(clock_1_out), ._8_bit_number(out_7));
  _1_to_256_Iterator u_1_to_256_iterator_2 (.Clock(clock_1_out), ._8_bit_number(out_11));
  _1_to_256_Iterator u_1_to_256_iterator_3 (.Clock(clock_1_out), ._8_bit_number(out_15));
  _1_to_256_Iterator u_1_to_256_iterator_4 (.Clock(clock_1_out), ._8_bit_number(out_19));
  _1_to_8_Iterator u_1_to_8_iterator_1 (.Clock(clock_1_out), ._8_bit_number(out_23));
  _1_to_256_Iterator u_1_to_256_iterator_5 (.Clock(clock_1_out), ._8_bit_number(out_28));
  _1_to_8_Iterator u_1_to_8_iterator_2 (.Clock(clock_1_out), ._8_bit_number(out_32));
  _1_to_8_Iterator u_1_to_8_iterator_3 (.Clock(clock_1_out), ._8_bit_number(out_36));
  ALU alu_1 (
    .X(out_7), .Y(8'h1), .State(3'b000), .Output(Output_2), .Unsigned_Overflow(Unsigned_Overflow_2),
    .Signed_Overflow(Signed_Overflow_2));
  ALU alu_2 (
    .X({8{1'b1}}), .Y(out_11), .State(3'b001), .Output(Output_3), .Unsigned_Overflow(Unsigned_Overflow_3),
    .Signed_Overflow(Signed_Overflow_3));
  ALU alu_3 (
    .X(out_15), .Y(8'haa), .State(3'b010), .Output(Output_4), .Unsigned_Overflow(Unsigned_Overflow_4),
    .Signed_Overflow(Signed_Overflow_4));
  ALU alu_4 (
    .X(out_19), .Y(8'haa), .State(3'b011), .Output(Output_5), .Unsigned_Overflow(Unsigned_Overflow_5),
    .Signed_Overflow(Signed_Overflow_5));
  ALU alu_5 (
    .X(8'h1), .Y(out_23), .State(3'b100), .Output(Output_6), .Unsigned_Overflow(Unsigned_Overflow_6),
    .Signed_Overflow(Signed_Overflow_6));
  ALU alu_6 (
    .X({8{1'b0}}), .Y(out_28), .State(3'b101), .Output(Output_7), .Unsigned_Overflow(Unsigned_Overflow_7),
    .Signed_Overflow(Signed_Overflow_7));
  ALU alu_7 (
    .X(8'h80), .Y(out_32), .State(3'b110), .Output(Output_8), .Unsigned_Overflow(Unsigned_Overflow_8),
    .Signed_Overflow(Signed_Overflow_8));
  ALU alu_8 (
    .X(8'h80), .Y(out_36), .State(3'b111), .Output(Output_9), .Unsigned_Overflow(Unsigned_Overflow_9),
    .Signed_Overflow(Signed_Overflow_9));
  ALU alu_9 (
    .X(in_1), .Y(in_2), .State(in_3), .Output(Output), .Unsigned_Overflow(Unsigned_Overflow),
    .Signed_Overflow(Signed_Overflow));

  assign SIGNED_LESS_THAN = {8{1'b0}};

  // Notes on the sheet:
  //   ADD
  //   SUB
  //   OR
  //   AND
  //   SLL
  //   SRL
  //   SRA
  //   TEST BENCH
  //   Our test bench has one mock up for each operation
  //   Each mock up uses an iteator to test evey possible value of input
endmodule

module ALU (
  input  [7:0] X,
  input  [7:0] Y,
  input  [2:0] State,
  output [7:0] Output,
  output Unsigned_Overflow,
  output Signed_Overflow
);

  wire n000_add_1_signed_overflow, n000_add_1_unsigned_overflow, n001_sub_1_signed_overflow,
       n001_sub_1_unsigned_overflow, n2to1_mux_1_bit_1_out_4, n2to1_mux_1_bit_2_out_4,
       n2to1_mux_1_bit_3_out_4, n2to1_mux_1_bit_5_out_4;
  wire [7:0] n000_add_1_output, n001_sub_1_output, n2to1_mux_8_bit_buses_1_output,
       n2to1_mux_8_bit_buses_2_output, n2to1_mux_8_bit_buses_3_output, n2to1_mux_8_bit_buses_4_output,
       n2to1_mux_8_bit_buses_5_output, n2to1_mux_8_bit_buses_6_output, n010_or_1_output, n011_and_1_output,
       n100_sll_1_output, n101_signed_less_than_1_output, n110_srl_1_output, n111_sra_1_output;

  _000_ADD u_000_add_1 (
    .X(X), .Y(Y), .Output(n000_add_1_output), .Unsigned_Overflow(n000_add_1_unsigned_overflow),
    .Signed_Overflow(n000_add_1_signed_overflow));
  _001_SUB u_001_sub_1 (
    .X(X), .Y(Y), .Output(n001_sub_1_output), .Unsigned_Overflow(n001_sub_1_unsigned_overflow),
    .Signed_Overflow(n001_sub_1_signed_overflow));
  _010_OR u_010_or_1 (.X(X), .Y(Y), .Output(n010_or_1_output));
  _011_AND u_011_and_1 (.X(X), .Y(Y), .Output(n011_and_1_output));
  _100_SLL u_100_sll_1 (.X(X), .Y(Y), .Output(n100_sll_1_output));
  _101_SIGNED_LESS_THAN u_101_signed_less_than_1 (.X(X), .Y(Y), .Output(n101_signed_less_than_1_output));
  _110_SRL u_110_srl_1 (.X(X), .Y(Y), .Output(n110_srl_1_output));
  _111_SRA u_111_sra_1 (.X(X), .Y(Y), .Output(n111_sra_1_output));
  _2to1_MUX__8_BIT_BUSES u_2to1_mux_8_bit_buses_1 (
    .X(n000_add_1_output), .Y(n001_sub_1_output), .Selector(State[0]), .Output(n2to1_mux_8_bit_buses_1_output));
  _2to1_MUX__8_BIT_BUSES u_2to1_mux_8_bit_buses_2 (
    .X(n2to1_mux_8_bit_buses_1_output), .Y(n2to1_mux_8_bit_buses_3_output), .Selector(State[1]),
    .Output(n2to1_mux_8_bit_buses_2_output));
  _2to1_MUX__8_BIT_BUSES u_2to1_mux_8_bit_buses_3 (
    .X(n010_or_1_output), .Y(n011_and_1_output), .Selector(State[0]), .Output(n2to1_mux_8_bit_buses_3_output));
  _2to1_MUX__8_BIT_BUSES u_2to1_mux_8_bit_buses_4 (
    .X(n100_sll_1_output), .Y(n101_signed_less_than_1_output), .Selector(State[0]),
    .Output(n2to1_mux_8_bit_buses_4_output));
  _2to1_MUX__8_BIT_BUSES u_2to1_mux_8_bit_buses_5 (
    .X(n2to1_mux_8_bit_buses_4_output), .Y(n2to1_mux_8_bit_buses_6_output), .Selector(State[1]),
    .Output(n2to1_mux_8_bit_buses_5_output));
  _2to1_MUX__8_BIT_BUSES u_2to1_mux_8_bit_buses_6 (
    .X(n110_srl_1_output), .Y(n111_sra_1_output), .Selector(State[0]), .Output(n2to1_mux_8_bit_buses_6_output));
  _2to1_MUX__8_BIT_BUSES u_2to1_mux_8_bit_buses_7 (
    .X(n2to1_mux_8_bit_buses_2_output), .Y(n2to1_mux_8_bit_buses_5_output), .Selector(State[2]),
    .Output(Output));
  _2to1_MUX__1_BIT u_2to1_mux_1_bit_1 (
    .a(n000_add_1_unsigned_overflow), .b(n001_sub_1_unsigned_overflow), .s(State[0]),
    .out_4(n2to1_mux_1_bit_1_out_4));
  _2to1_MUX__1_BIT u_2to1_mux_1_bit_2 (
    .a(n000_add_1_signed_overflow), .b(n001_sub_1_signed_overflow), .s(State[0]),
    .out_4(n2to1_mux_1_bit_2_out_4));
  _2to1_MUX__1_BIT u_2to1_mux_1_bit_3 (
    .a(n2to1_mux_1_bit_1_out_4), .b(1'b0), .s(State[1]), .out_4(n2to1_mux_1_bit_3_out_4));
  _2to1_MUX__1_BIT u_2to1_mux_1_bit_4 (.a(n2to1_mux_1_bit_3_out_4), .b(1'b0), .s(State[2]), .out_4(Unsigned_Overflow));
  _2to1_MUX__1_BIT u_2to1_mux_1_bit_5 (
    .a(n2to1_mux_1_bit_2_out_4), .b(1'b0), .s(State[1]), .out_4(n2to1_mux_1_bit_5_out_4));
  _2to1_MUX__1_BIT u_2to1_mux_1_bit_6 (.a(n2to1_mux_1_bit_5_out_4), .b(1'b0), .s(State[2]), .out_4(Signed_Overflow));

  // Notes on the sheet:
  //   ADD
  //   SUB
  //   OR
  //   AND
  //   SLL
  //   Signed LT
  //   SRL
  //   SRA
  //   Put your solution here. Do NOT add any more inputs/outputs that face EAST or WEST
  //   You may move the inputs in this circuit around but do NOT change their facing
  //   Cascade of MUXes
  //   Looks at the LSB bit first
endmodule

module _000_ADD (
  input  [7:0] X,
  input  [7:0] Y,
  output [7:0] Output,
  output Unsigned_Overflow,
  output Signed_Overflow
);

  _8bitadder u_8bitadder_1 (
    .X(X), .Y(Y), .Carry_in(1'b0), .Output(Output), .Unsigned_Overflow(Unsigned_Overflow),
    .Signed_Overflow(Signed_Overflow));

  // Notes on the sheet:
  //   Add
  //   Uses the 8 bit adder with no carry-in value
endmodule

module _001_SUB (
  input  [7:0] X,
  input  [7:0] Y,
  output [7:0] Output,
  output Unsigned_Overflow,
  output Signed_Overflow
);

  _8bitadder u_8bitadder_1 (
    .X(X), .Y(Y), .Carry_in(1'b1), .Output(Output), .Signed_Overflow(Signed_Overflow));  // open: Unsigned_Overflow

  assign Unsigned_Overflow = 1'b0;

  // Notes on the sheet:
  //   8 Bit Adder
  //   Subtract
  //   Subtract uses the 8 bit adder. It triggers the adder with a carry-in value of 1.
  //   This causes the adder to invert Y and add the 1-bit carry-in
  //   Since two numbers subtracted from each other can never cause unsigned overflow, we ground that contact.
endmodule

module _010_OR (
  input  [7:0] X,
  input  [7:0] Y,
  output [7:0] Output
);

  or or_1 (Output[0], X[0], Y[0]);
  or or_2 (Output[1], X[1], Y[1]);
  or or_3 (Output[2], X[2], Y[2]);
  or or_4 (Output[3], X[3], Y[3]);
  or or_5 (Output[4], X[4], Y[4]);
  or or_6 (Output[5], X[5], Y[5]);
  or or_7 (Output[6], X[6], Y[6]);
  or or_8 (Output[7], X[7], Y[7]);

  // Notes on the sheet:
  //   This is a stupid way to do it though, since we can use Logisim with 8 bit buses... Oh well, good practice!
  //   8 BIT BITWISE OR
  //   or
  //   or
  //   or
  //   or
  //   or
  //   or
  //   or
  //   or
endmodule

module _011_AND (
  input  [7:0] X,
  input  [7:0] Y,
  output [7:0] Output
);

  and and_1 (Output[0], X[0], Y[0]);
  and and_2 (Output[1], X[1], Y[1]);
  and and_3 (Output[2], X[2], Y[2]);
  and and_4 (Output[3], X[3], Y[3]);
  and and_5 (Output[4], X[4], Y[4]);
  and and_6 (Output[5], X[5], Y[5]);
  and and_7 (Output[6], X[6], Y[6]);
  and and_8 (Output[7], X[7], Y[7]);

  // Notes on the sheet:
  //   8 BIT BITWISE AND
  //   Just about identical to 8 bit OR!
  //   and
  //   and
  //   and
  //   and
  //   and
  //   and
  //   and
  //   and
endmodule

module _100_SLL (
  input  [7:0] X,
  input  [7:0] Y,
  output [7:0] Output
);

  wire or_1_out;
  wire [7:0] n2to1_mux_8_bit_buses_1_output, n2to1_mux_8_bit_buses_2_output, n2to1_mux_8_bit_buses_3_output;

  or or_1 (or_1_out, Y[3], Y[4], Y[5], Y[6], Y[7]);
  _2to1_MUX__8_BIT_BUSES u_2to1_mux_8_bit_buses_1 (
    .X(X), .Y({X[6:0], 1'b0}), .Selector(Y[0]), .Output(n2to1_mux_8_bit_buses_1_output));
  _2to1_MUX__8_BIT_BUSES u_2to1_mux_8_bit_buses_2 (
    .X(n2to1_mux_8_bit_buses_1_output), .Y({n2to1_mux_8_bit_buses_1_output[5:0], 2'b00}), .Selector(Y[1]),
    .Output(n2to1_mux_8_bit_buses_2_output));
  _2to1_MUX__8_BIT_BUSES u_2to1_mux_8_bit_buses_3 (
    .X(n2to1_mux_8_bit_buses_2_output), .Y({n2to1_mux_8_bit_buses_2_output[3:0], 4'b0000}), .Selector(Y[2]),
    .Output(n2to1_mux_8_bit_buses_3_output));
  _2to1_MUX__8_BIT_BUSES u_2to1_mux_8_bit_buses_4 (
    .X(n2to1_mux_8_bit_buses_3_output), .Y({8{1'b0}}), .Selector(or_1_out), .Output(Output));

  // Notes on the sheet:
  //   looks at first bit
  //   Shifts by 1
  //   mux
  //   looks at second bit
  //   looks at third bit
  //   Shift Left Logical
  //   By using a 1 bit, 2 bit and 4 bit shift along with muxes that enables to disables each, we can model any shift from 1 to 7 bits.
  //   more than 7 bits of shifting will result in all zeros, so we hardcode that case.
  //   For no shift, we use the first mux connected to the input case.
  //   mux
  //   Shifts by 2
  //   Shifts by 4
  //   mux
  //   mux
endmodule

module _101_SIGNED_LESS_THAN (
  input  [7:0] X,
  input  [7:0] Y,
  output [7:0] Output
);

  wire n001_sub_1_signed_overflow;
  wire [7:0] n001_sub_1_output;

  _001_SUB u_001_sub_1 (
    .X(X), .Y(Y), .Output(n001_sub_1_output), .Signed_Overflow(n001_sub_1_signed_overflow));  // open: Unsigned_Overflow
  xor xor_1 (Output[0], n001_sub_1_output[7], n001_sub_1_signed_overflow);

  assign Output[7:1] = {7{1'b0}};

  // Notes on the sheet:
  //   sub
  //   xor
  //   Set Less Than
  //   Subtracts x from y and look at the most significant bit.
  //   Since this represents the sign, we can make an easy judgement about the relative magnitudes of X and Y
  //   We need to keep in mind that overflow can occur. This has the effect of reversing the truth table values.
  //   We use an XOR to account for this effect, since XOR is a conditional inverter, which is what we need
endmodule

module _110_SRL (
  input  [7:0] X,
  input  [7:0] Y,
  output [7:0] Output
);

  shift_right_generic shift_right_generic_1 (.X(X), .Y(Y), .Extend_With(1'b0), .Output(Output));

  // Notes on the sheet:
  //   shift right generic
  //   Shift Right Logical
  //   We use our generic right shifter and feed it with a 0 as the value to extend with.
endmodule

module _111_SRA (
  input  [7:0] X,
  input  [7:0] Y,
  output [7:0] Output
);

  shift_right_generic shift_right_generic_1 (.X(X), .Y(Y), .Extend_With(X[7]), .Output(Output));

  // Notes on the sheet:
  //   selects most significant bit
  //   Shift Right Arithmetically
  //   We feed our general right shifter with the most significant bit of our input X (the value to be shifted)
  //   This creates the effect of sign-extending with number
  //   shift right generic
endmodule

module _2to1_MUX__8_BIT_BUSES (
  input  [7:0] X,
  input  [7:0] Y,
  input  Selector,
  output [7:0] Output
);

  wire [7:0] and_1_out, and_2_out, not_1_out;

  assign and_1_out = X & not_1_out;  // AND_Gate and_1, 8 bits wide
  assign not_1_out = ~{8{Selector}};  // NOT_Gate not_1, 8 bits wide
  assign and_2_out = Y & {8{Selector}};  // AND_Gate and_2, 8 bits wide
  assign Output = and_1_out | and_2_out;  // OR_Gate or_1, 8 bits wide

  // Notes on the sheet:
  //   This is a very strightforward mux that selects between two input buses based on a selector bit.
  //   and
  //   and
  //   8 bit wide 2 input buses to one output bus Mux
  //   or
endmodule

module shift_right_generic (
  input  [7:0] X,
  input  [7:0] Y,
  input  Extend_With,
  output [7:0] Output
);

  wire or_1_out;
  wire [7:0] n2to1_mux_8_bit_buses_1_output, n2to1_mux_8_bit_buses_2_output, n2to1_mux_8_bit_buses_3_output;

  or or_1 (or_1_out, Y[3], Y[4], Y[5], Y[6], Y[7]);
  _2to1_MUX__8_BIT_BUSES u_2to1_mux_8_bit_buses_1 (
    .X(X), .Y({Extend_With, X[7:1]}), .Selector(Y[0]), .Output(n2to1_mux_8_bit_buses_1_output));
  _2to1_MUX__8_BIT_BUSES u_2to1_mux_8_bit_buses_2 (
    .X(n2to1_mux_8_bit_buses_1_output), .Y({{2{Extend_With}}, n2to1_mux_8_bit_buses_1_output[7:2]}),
    .Selector(Y[1]), .Output(n2to1_mux_8_bit_buses_2_output));
  _2to1_MUX__8_BIT_BUSES u_2to1_mux_8_bit_buses_3 (
    .X(n2to1_mux_8_bit_buses_2_output), .Y({{4{Extend_With}}, n2to1_mux_8_bit_buses_2_output[7:4]}),
    .Selector(Y[2]), .Output(n2to1_mux_8_bit_buses_3_output));
  _2to1_MUX__8_BIT_BUSES u_2to1_mux_8_bit_buses_4 (
    .X(n2to1_mux_8_bit_buses_3_output), .Y({8{Extend_With}}), .Selector(or_1_out), .Output(Output));

  // Notes on the sheet:
  //   Shifts by 1
  //   mux
  //   Generic Shift Right
  //   Shifts right by a specified amount by looking at the 3 least significant bits of Y
  //   The algorithm is related to the one explained in SLL
  //   By using an "Extend With" input, we can change this to be either a logical or arithmetical shift
  //   Shifts by 2
  //   mux
  //   Shifts by 3
  //   mux
  //   mux
endmodule

module majority (
  input  A,
  input  B,
  input  C,
  output O
);

  wire and_1_out, and_2_out, and_3_out;

  and and_1 (and_1_out, A, B);
  and and_2 (and_2_out, B, C);
  and and_3 (and_3_out, C, A);
  or or_1 (O, and_1_out, and_2_out, and_3_out);

  // Notes on the sheet:
  //   and
  //   and
  //   and
  //   Majority
  //   MAJORITY - Outputs 1 if two of the three inputs is 1
  //   or
endmodule

module _1bitadder (
  input  A,
  input  B,
  input  C_in,
  output Sum,
  output C_out
);

  majority majority_1 (.A(A), .B(B), .C(C_in), .O(C_out));
  xor odd_parity_1 (Sum, A, B, C_in);

  // Notes on the sheet:
  //   carry-in
  //   Creates the sum and carry-out values from the carry in and to-be-added a and b bits
  //   One Bit Adder
  //   majority
  //   odd parity - XOR
  //   sum of a and b for current bit
  //   carry-out
endmodule

module _8bitadder (
  input  [7:0] X,
  input  [7:0] Y,
  input  Carry_in,
  output [7:0] Output,
  output Unsigned_Overflow,
  output Signed_Overflow
);

  wire n1bitadder_1_c_out, n1bitadder_2_c_out, n1bitadder_3_c_out, n1bitadder_4_c_out, n1bitadder_5_c_out,
       n1bitadder_6_c_out, n1bitadder_7_c_out;
  wire [7:0] xor_1_out;

  assign xor_1_out = Y ^ {8{Carry_in}};  // XOR_Gate xor_1, 8 bits wide
  _1bitadder u_1bitadder_1 (.A(X[0]), .B(xor_1_out[0]), .C_in(Carry_in), .Sum(Output[0]), .C_out(n1bitadder_1_c_out));
  _1bitadder u_1bitadder_2 (
    .A(X[1]), .B(xor_1_out[1]), .C_in(n1bitadder_1_c_out), .Sum(Output[1]), .C_out(n1bitadder_2_c_out));
  _1bitadder u_1bitadder_3 (
    .A(X[2]), .B(xor_1_out[2]), .C_in(n1bitadder_2_c_out), .Sum(Output[2]), .C_out(n1bitadder_3_c_out));
  _1bitadder u_1bitadder_4 (
    .A(X[3]), .B(xor_1_out[3]), .C_in(n1bitadder_3_c_out), .Sum(Output[3]), .C_out(n1bitadder_4_c_out));
  _1bitadder u_1bitadder_5 (
    .A(X[4]), .B(xor_1_out[4]), .C_in(n1bitadder_4_c_out), .Sum(Output[4]), .C_out(n1bitadder_5_c_out));
  _1bitadder u_1bitadder_6 (
    .A(X[5]), .B(xor_1_out[5]), .C_in(n1bitadder_5_c_out), .Sum(Output[5]), .C_out(n1bitadder_6_c_out));
  _1bitadder u_1bitadder_7 (
    .A(X[6]), .B(xor_1_out[6]), .C_in(n1bitadder_6_c_out), .Sum(Output[6]), .C_out(n1bitadder_7_c_out));
  _1bitadder u_1bitadder_8 (
    .A(X[7]), .B(xor_1_out[7]), .C_in(n1bitadder_7_c_out), .Sum(Output[7]), .C_out(Unsigned_Overflow));
  xor xor_2 (Signed_Overflow, Unsigned_Overflow, n1bitadder_7_c_out);

  // Notes on the sheet:
  //   XOR for subtraction
  //   1 bit adder
  //   8 bit Adder/Subtractor
  //   Uses 8 one-bit adders with cascaded carry-ins and carry-outs to implement an 8 bit adder.
  //   Uses an XOR and input carry-in value to create a subtractor
  //   Unsigned overflow occurs when carry-out from the last adder is present
  //   Signed overflow occurs when there is carry-out from only one of the last two adders
  //   1 bit adder
  //   1 bit adder
  //   1 bit adder
  //   1 bit adder
  //   1 bit adder
  //   1 bit adder
  //   1 bit adder
  //   XOR for signed overflow
endmodule

module _1_to_256_Iterator (
  input  Clock,
  output [7:0] _8_bit_number
);

  wire [7:0] adder_1_out;

  Adder #(.width(8)) adder_1 (.a(8'h1), .b(_8_bit_number), .out(adder_1_out));  // open: cin, cout
  Register #(.width(8)) register_1 (.D(adder_1_out), .Q(_8_bit_number), .clk(Clock));  // open: en, clr

  // Notes on the sheet:
  //   Iterator
  //   Counts up from 0 to 2^8
endmodule

module _1_to_8_Iterator (
  input  Clock,
  output [7:0] _8_bit_number
);

  wire [7:0] adder_1_out;

  Adder #(.width(8)) adder_1 (.a(8'h1), .b(_8_bit_number), .out(adder_1_out));  // open: cin, cout
  Register #(.width(8)) register_1 (
    .D(adder_1_out), .Q(_8_bit_number), .clk(Clock), .clr(_8_bit_number[3]));  // open: en

  // Notes on the sheet:
  //   Iterator
  //   Counts up from 0 to 8
  //   Spliiter resets on bit 4 coming live
endmodule

module _2to1_MUX__1_BIT (
  input  a,
  input  b,
  input  s,
  output out_4
);

  wire and_1_out, and_2_out, not_1_out;

  not not_1 (not_1_out, s);
  and and_1 (and_1_out, a, not_1_out);
  and and_2 (and_2_out, b, s);
  or or_1 (out_4, and_1_out, and_2_out);

  // Notes on the sheet:
  //   This is a very strightforward mux that selects between two input buses based on a selector bit.
  //   1 bit wide 2 input buses to one output bus Mux
endmodule

module max (
  input  [7:0] in_1,
  input  [7:0] in_2,
  output [7:0] out_3
);

  wire [7:0] n101_signed_less_than_1_output;

  _101_SIGNED_LESS_THAN u_101_signed_less_than_1 (.X(in_1), .Y(in_2), .Output(n101_signed_less_than_1_output));
  _2to1_MUX__8_BIT_BUSES u_2to1_mux_8_bit_buses_1 (
    .X(in_1), .Y(in_2), .Selector(n101_signed_less_than_1_output[0]), .Output(out_3));

  // Notes on the sheet:
  //   Max
  //   Returns the larger of the two inputs
endmodule

module min (
  input  [7:0] in_1,
  input  [7:0] in_2,
  output [7:0] out_3
);

  wire not_1_out;
  wire [7:0] n101_signed_less_than_1_output;

  _101_SIGNED_LESS_THAN u_101_signed_less_than_1 (.X(in_1), .Y(in_2), .Output(n101_signed_less_than_1_output));
  not not_1 (not_1_out, n101_signed_less_than_1_output[0]);
  _2to1_MUX__8_BIT_BUSES u_2to1_mux_8_bit_buses_1 (.X(in_1), .Y(in_2), .Selector(not_1_out), .Output(out_3));

  // Notes on the sheet:
  //   Min
  //   Returns the smaller of the two inputs
endmodule
