// Logisim project cpu.circ as structural Verilog: 12 circuits, main circuit 8-bit CPU
module _8_bit_CPU (
  output [7:0] r0,
  output [7:0] r1,
  output [7:0] rd,
  output [7:0] rs,
  output [7:0] out_5,
  output [4:0] Jump,
  output [1:0] RA,
  output [1:0] out_8,
  output [3:0] Disp
);

  wire and_1_out, blockbottom_1_out_5, blockbottom_1_out_6, blockbottom_1_out_7, blockbottom_1_out_8,
       blockbottom_1_out_9, blockbottom_1_out_10, blockbottom_1_out_11, blockbottom_1_out_12,
       blockbottom_1_out_13, blockbottom_1_out_14, blockbottom_1_out_15, blockbottom_1_out_16,
       blockbottom_1_out_17, blockbottom_1_out_18, blockbottom_1_out_19, blockbottom_1_out_20,
       blocktop_1_out_5, blocktop_1_out_6, blocktop_1_out_7, blocktop_1_out_8, blocktop_1_out_9,
       blocktop_1_out_10, blocktop_1_out_11, blocktop_1_out_12, blocktop_1_out_13, blocktop_1_out_14,
       blocktop_1_out_15, blocktop_1_out_16, blocktop_1_out_17, blocktop_1_out_18, blocktop_1_out_19,
       blocktop_1_out_20, button_1_out, clock_1_out, clock_2_out, clock_3_out, comparator_1_eq,
       control_1_out_3, control_1_out_4, control_1_out_5, control_1_out_8, control_1_out_9, control_1_out_10,
       control_1_out_11, control_1_out_12, control_1_out_13, control_1_out_14, not_1_out;
  wire [1:0] multiplexer_4_out, multiplexer_5_out, multiplexer_6_out;
  wire [7:0] adder_1_out, adder_2_out, alu_1_output, branch_1_new_pc, controlled_buffer_1_out,
       display_1_out_5, display_1_out_6, display_1_out_7, display_1_out_8, jump_1_new_pc, multiplexer_1_out,
       multiplexer_2_out, multiplexer_3_out, multiplexer_7_out, multiplexer_8_out, multiplexer_9_out,
       ram_1_data, register_1_q, registerfile_1_busa, registerfile_1_busb, zeroextend4to8_1_out_2;

  LED led_1 (.in(clock_1_out));
  Clock #(.highDuration(2), .lowDuration(1)) clock_1 (.out(clock_1_out));
  Clock #(.highDuration(1), .lowDuration(1)) clock_2 (.out(clock_2_out));
  LED led_2 (.in(clock_1_out));
  Button button_1 (.out(button_1_out));
  LED led_3 (.in(clock_2_out));
  LED led_4 (.in(clock_2_out));
  Register #(.width(8)) register_1 (
    .D(multiplexer_3_out), .Q(register_1_q), .clk(clock_3_out), .clr(button_1_out));  // open: en
  Adder #(.width(8)) adder_1 (.a(register_1_q), .b(8'h1), .out(adder_1_out));  // open: cin, cout
  Multiplexer #(.select(1), .width(8)) multiplexer_1 (
    .in0(adder_1_out), .in1(adder_2_out), .out(multiplexer_1_out), .sel(and_1_out));
  Adder #(.width(8)) adder_2 (.a(adder_1_out), .b(branch_1_new_pc), .out(adder_2_out));  // open: cin, cout
  and and_1 (and_1_out, control_1_out_3, comparator_1_eq);
  Clock #(.highDuration(1), .lowDuration(1)) clock_3 (.out(clock_3_out));
  LED led_5 (.in(clock_1_out));
  LED led_6 (.in(clock_2_out));
  LED led_7 (.in(clock_2_out));
  LED led_8 (.in(clock_1_out));
  Multiplexer #(.select(1), .width(8)) multiplexer_2 (
    .in0(multiplexer_1_out), .in1(jump_1_new_pc), .out(multiplexer_2_out), .sel(control_1_out_4));
  ROM #(.addrWidth(8), .dataWidth(8)) rom_1 (.addr(register_1_q), .data({out_5[7:5], Jump}), .sel(1'b1));
  Multiplexer #(.select(1), .width(8)) multiplexer_3 (
    .in0(multiplexer_2_out), .in1(alu_1_output), .out(multiplexer_3_out), .sel(control_1_out_5));
  jump jump_1 (.Address(Jump), .in_2(register_1_q), .New_PC(jump_1_new_pc));
  branch branch_1 (.Address(Jump), .New_PC(branch_1_new_pc));
  ZeroExtend4to8 zeroextend4to8_1 (.in_1(Jump[3:0]), .out_2(zeroextend4to8_1_out_2));
  Control control_1 (
    .Opcode(out_5[7:5]), .Funct(Jump[3:0]), .out_3(control_1_out_3), .out_4(control_1_out_4),
    .out_5(control_1_out_5), .out_6(RA), .out_7(out_8), .out_8(control_1_out_8), .out_9(control_1_out_9),
    .out_10(control_1_out_10), .out_11(control_1_out_11), .out_12(control_1_out_12),
    .out_13(control_1_out_13), .out_14(control_1_out_14));
  Multiplexer #(.select(2), .width(2)) multiplexer_4 (
    .in0(2'b10), .in1({1'b0, Jump[4]}), .in2(2'b11), .in3(2'b11), .out(multiplexer_4_out), .sel(RA));
  Multiplexer #(.select(2), .width(2)) multiplexer_5 (
    .in0({1'b0, Jump[4]}), .in1(2'b01), .in2(2'b10), .in3(2'b10), .out(multiplexer_5_out), .sel(out_8));
  Multiplexer #(.select(1), .width(2)) multiplexer_6 (
    .in0(2'b11), .in1(2'b00), .out(multiplexer_6_out), .sel(control_1_out_8));
  RegisterFile registerfile_1 (
    .Data_to_write(multiplexer_9_out), .RW(multiplexer_4_out), .RA(multiplexer_6_out),
    .RB(multiplexer_5_out), .Reset(button_1_out), .r0(r0), .r1(r1), .rd(rd), .rs(rs), .in_6(control_1_out_9),
    .in_7(clock_3_out), .busA(registerfile_1_busa), .busB(registerfile_1_busb));
  _7_Segment_Display u_7_segment_display_1 (
    .g(blocktop_1_out_5), .f(blocktop_1_out_13), .a(blocktop_1_out_14), .b(blocktop_1_out_6),
    .e(blockbottom_1_out_13), .d(blockbottom_1_out_5), .c(blockbottom_1_out_6), .dp(blockbottom_1_out_14));
  BlockBottom blockbottom_1 (
    .out_13(blockbottom_1_out_13), .out_5(blockbottom_1_out_5), .out_6(blockbottom_1_out_6),
    .out_14(blockbottom_1_out_14), .out_15(blockbottom_1_out_15), .out_7(blockbottom_1_out_7),
    .out_8(blockbottom_1_out_8), .out_16(blockbottom_1_out_16), .out_17(blockbottom_1_out_17),
    .out_9(blockbottom_1_out_9), .out_10(blockbottom_1_out_10), .out_18(blockbottom_1_out_18),
    .out_19(blockbottom_1_out_19), .out_11(blockbottom_1_out_11), .out_12(blockbottom_1_out_12),
    .out_20(blockbottom_1_out_20), .in_1(display_1_out_5), .in_2(display_1_out_6), .in_3(display_1_out_7),
    .in_4(display_1_out_8));
  Multiplexer #(.select(1), .width(8)) multiplexer_7 (
    .in0(registerfile_1_busa), .in1(zeroextend4to8_1_out_2), .out(multiplexer_7_out), .sel(control_1_out_10));
  Multiplexer #(.select(1), .width(8)) multiplexer_8 (
    .in0(registerfile_1_busb), .in1(8'h4), .out(multiplexer_8_out), .sel(control_1_out_11));
  ControlALU controlalu_1 (.Opcode(out_5[7:5]), .Funct(Jump[3:0]), .out_3(Disp));
  BlockTop blocktop_1 (
    .in_1(display_1_out_5), .in_2(display_1_out_6), .in_3(display_1_out_7), .in_4(display_1_out_8),
    .out_5(blocktop_1_out_5), .out_13(blocktop_1_out_13), .out_14(blocktop_1_out_14),
    .out_6(blocktop_1_out_6), .out_7(blocktop_1_out_7), .out_15(blocktop_1_out_15),
    .out_16(blocktop_1_out_16), .out_8(blocktop_1_out_8), .out_9(blocktop_1_out_9),
    .out_17(blocktop_1_out_17), .out_18(blocktop_1_out_18), .out_10(blocktop_1_out_10),
    .out_11(blocktop_1_out_11), .out_19(blocktop_1_out_19), .out_20(blocktop_1_out_20),
    .out_12(blocktop_1_out_12));
  _7_Segment_Display u_7_segment_display_2 (
    .g(blocktop_1_out_9), .f(blocktop_1_out_17), .a(blocktop_1_out_18), .b(blocktop_1_out_10),
    .e(blockbottom_1_out_17), .d(blockbottom_1_out_9), .c(blockbottom_1_out_10), .dp(blockbottom_1_out_18));
  _7_Segment_Display u_7_segment_display_3 (
    .g(blocktop_1_out_7), .f(blocktop_1_out_15), .a(blocktop_1_out_16), .b(blocktop_1_out_8),
    .e(blockbottom_1_out_15), .d(blockbottom_1_out_7), .c(blockbottom_1_out_8), .dp(blockbottom_1_out_16));
  Display display_1 (
    .Clear(button_1_out), .out_5(display_1_out_5), .out_6(display_1_out_6), .out_7(display_1_out_7),
    .out_8(display_1_out_8), .Display_Value(controlled_buffer_1_out), .Imm(zeroextend4to8_1_out_2),
    .Display(clock_3_out));
  assign controlled_buffer_1_out = control_1_out_14 ? alu_1_output : 8'bz;  // Controlled_Buffer controlled_buffer_1
  ALU alu_1 (.in_1(multiplexer_7_out), .Input_B(multiplexer_8_out), .Funct(Disp), .Output(alu_1_output));
  _7_Segment_Display u_7_segment_display_4 (
    .g(blocktop_1_out_11), .f(blocktop_1_out_19), .a(blocktop_1_out_20), .b(blocktop_1_out_12),
    .e(blockbottom_1_out_19), .d(blockbottom_1_out_11), .c(blockbottom_1_out_12), .dp(blockbottom_1_out_20));
  Comparator #(.width(8), .mode("twosComplement")) comparator_1 (
    .a(alu_1_output), .b({8{1'b0}}), .eq(comparator_1_eq));  // open: gt, lt
  RAM #(.addrWidth(8), .dataWidth(8)) ram_1 (
    .addr(alu_1_output), .data(ram_1_data), .sel(1'b1), .clk(clock_3_out), .ld(not_1_out), .clr(button_1_out));
  not not_1 (not_1_out, control_1_out_12);
  assign ram_1_data = control_1_out_12 ? registerfile_1_busa : 8'bz;  // Controlled_Buffer controlled_buffer_2
  Multiplexer #(.select(1), .width(8)) multiplexer_9 (
    .in0(alu_1_output), .in1(ram_1_data), .out(multiplexer_9_out), .sel(control_1_out_13));

  assign out_5[4:0] = Jump;

  // Notes on the sheet:
  //   RESET
  //   Niels Joubert
  //   CS61C-CA
  //   18275309
  //   PC
  //   branch
  //   Jump
  //   InstMemory
  //   $rx
  //   contents of rom_1 (hex, n*v repeats v):
  //   40 8 60 8 80 8 40 18 75 18 9 14 a 16 18 30 40 18 72 18 9 14 8 40 18 75 18 9 16 8 21 40 8 60 8 80 8
  //   40 18 76 18 9 16 8 22 4f 8 6f 8 23 18 ff
  //   beq
  //   JR
  //   Register Values
  //   Ext
  //   Opcode
  //   Funct
  //   address
  //   Imm
  //   $rd
  //   $rs
  //   $rs
  //   $rx
  //   $r1
  //   $rd
  //   RegDest
  //   8 Bit Processor
  //   RegFile
  //   busW
  //   RW
  //   RA
  //   $r0
  //   $rs
  //   RegWrite
  //   RB
  //   RA
  //   Control
  //   A
  //   B
  //   RB
  //   ALU-A-Src
  //   ALU-B-Src
  //   DISP[3]
  //   DISP[1]
  //   DISP[2]
  //   DISP[2]
  //   Display
  //   ALU
  //   ALUctr
  //   DISP[0]
  //   DataMemory
  //   memwrite
  //   MemToReg
endmodule

module InstMem (
  input  [7:0] Address,
  output [7:0] DataOut
);

  ROM #(.addrWidth(8), .dataWidth(8)) rom_1 (.addr(Address), .data(DataOut), .sel(1'b1));

  // Notes on the sheet:
  //   Setup your Instruction Memory Module here.
  //   contents of rom_1 (hex, n*v repeats v):
  //   0 2 0 0 0 54 c5
endmodule

module DataMem (
  input  [7:0] DataIn,
  input  [7:0] Address,
  input  MemWrite,
  input  Reset,
  output [7:0] DataOut
);

  wire clock_1_out, not_1_out;

  assign DataOut = MemWrite ? DataIn : 8'bz;  // Controlled_Buffer controlled_buffer_1
  not not_1 (not_1_out, MemWrite);
  Clock #(.highDuration(1), .lowDuration(1)) clock_1 (.out(clock_1_out));
  RAM #(.addrWidth(8), .dataWidth(8)) ram_1 (
    .addr(Address), .data(DataOut), .sel(1'b1), .clk(clock_1_out), .ld(not_1_out), .clr(Reset));

  // Notes on the sheet:
  //   Setup your Data Memory Module here.
endmodule

module RegisterFile (
  input  Reset,
  input  [7:0] Data_to_write,
  input  [1:0] RW,
  input  [1:0] RA,
  input  [1:0] RB,
  input  in_6,
  input  in_7,
  output [7:0] r0,
  output [7:0] r1,
  output [7:0] rd,
  output [7:0] rs,
  output [7:0] busA,
  output [7:0] busB
);

  wire [7:0] controlled_buffer_1_out, demultiplexer_1_out0, demultiplexer_1_out1, demultiplexer_1_out2,
       demultiplexer_1_out3;

  assign controlled_buffer_1_out = in_6 ? Data_to_write : 8'bz;  // Controlled_Buffer controlled_buffer_1
  Demultiplexer #(.select(2), .width(8), .tristate("true")) demultiplexer_1 (
    .out0(demultiplexer_1_out0), .out1(demultiplexer_1_out1), .out2(demultiplexer_1_out2),
    .out3(demultiplexer_1_out3), .in(controlled_buffer_1_out), .sel(RW));
  Register #(.width(8)) register_1 (.D(demultiplexer_1_out0), .Q(r0), .clk(in_7), .clr(Reset));  // open: en
  Register #(.width(8)) register_2 (.D(demultiplexer_1_out1), .Q(r1), .clk(in_7), .clr(Reset));  // open: en
  Register #(.width(8)) register_3 (.D(demultiplexer_1_out2), .Q(rd), .clk(in_7), .clr(Reset));  // open: en
  Register #(.width(8)) register_4 (.D(demultiplexer_1_out3), .Q(rs), .clk(in_7), .clr(Reset));  // open: en
  Multiplexer #(.select(2), .width(8)) multiplexer_1 (.in0(r0), .in1(r1), .in2(rd), .in3(rs), .out(busA), .sel(RA));
  Multiplexer #(.select(2), .width(8)) multiplexer_2 (.in0(r0), .in1(r1), .in2(rd), .in3(rs), .out(busB), .sel(RB));

  // Notes on the sheet:
  //   busW
  //   ReqWrite
  //   Register File
  //   $r0
  //   $r1
  //   $rd
  //   $rs
  //   Clock
endmodule

module ALU (
  input  [7:0] in_1,
  input  [7:0] Input_B,
  input  [3:0] Funct,
  output [7:0] Output
);

  wire not_2_out;
  wire [7:0] alu_1_output, buffer_1_out, max_1_out_3, min_1_out_3, multiplexer_1_out, negator_1_out,
       not_1_out;

  assign buffer_1_out = Input_B;  // Buffer buffer_1, 8 bits wide
  assign not_1_out = ~Input_B;  // NOT_Gate not_1, 8 bits wide
  Negator #(.width(8)) negator_1 (.in(Input_B), .out(negator_1_out));
  min min_1 (.in_1(in_1), .in_2(Input_B), .out_3(min_1_out_3));
  max max_1 (.in_1(in_1), .in_2(Input_B), .out_3(max_1_out_3));
  alu_ALU alu_1 (
    .X(in_1), .Y(Input_B), .State(Funct[2:0]), .Output(alu_1_output));  // open: Unsigned_Overflow, Signed_Overflow
  Multiplexer #(.select(3), .width(8)) multiplexer_1 (
    .in0(buffer_1_out), .in1(buffer_1_out), .in2(buffer_1_out), .in3(not_1_out), .in4(negator_1_out),
    .in5(buffer_1_out), .in6(min_1_out_3), .in7(max_1_out_3), .out(multiplexer_1_out), .sel(Funct[2:0]));
  Multiplexer #(.select(1), .width(8)) multiplexer_2 (
    .in0(multiplexer_1_out), .in1(alu_1_output), .out(Output), .sel(not_2_out));
  not not_2 (not_2_out, Funct[3]);

  // Notes on the sheet:
  //   Input A
  //   State:
  //   0-7
  //   8-10
  //   11
  //   12
  //   13
  //   14
  //   15
  //   on to simple ALU
  //   pass through
  //   not
  //   negate
  //   pass through
  //   min
  //   max
  //   Move, JR
  //   Not
  //   Negate
  //   min
  //   max
  //   R[$rd] = min(R[$rs], R[$rx])
  //   R[$rd] = max(R[$rs], R[$rx])
  //   ALU for Single Cycle CPU
  //   Simple ALU
endmodule

module TestComponents (
  input  [1:0] in_1,
  input  [1:0] RegisterFileTest,
  input  [1:0] in_3,
  input  in_4,
  input  [7:0] in_5,
  output [7:0] out_6,
  output [7:0] out_7
);

  // RegisterFile registerfile_1: pin names not known; wires that end beside it: in_5, in_4, in_1, RegisterFileTest, in_3, out_6, out_7
endmodule

module Control (
  input  [2:0] Opcode,
  input  [3:0] Funct,
  output out_3,
  output out_4,
  output out_5,
  output [1:0] out_6,
  output [1:0] out_7,
  output out_8,
  output out_9,
  output out_10,
  output out_11,
  output out_12,
  output out_13,
  output out_14
);

  wire and_4_out, and_5_out, and_8_out, and_11_out, and_17_out, and_18_out, and_19_out, and_20_out,
       and_21_out, and_22_out, and_23_out, not_2_out, not_3_out, not_4_out, not_5_out, not_6_out, not_7_out,
       not_8_out, not_9_out, not_10_out, not_11_out, not_12_out, not_13_out, not_14_out, not_15_out,
       not_16_out, not_17_out, not_18_out, not_19_out, not_20_out, not_21_out, not_22_out, not_23_out,
       not_24_out, not_25_out, not_26_out, not_27_out, not_28_out, not_29_out, not_30_out, not_31_out,
       or_2_out, xor_1_out, xor_2_out, xor_3_out;
  wire [2:0] not_1_out;

  assign not_1_out = ~Opcode;  // NOT_Gate not_1, 3 bits wide
  not not_2 (not_2_out, Opcode[2]);
  not not_3 (not_3_out, Opcode[1]);
  not not_4 (not_4_out, Opcode[0]);
  not not_5 (not_5_out, Funct[2]);
  not not_6 (not_6_out, Opcode[2]);
  not not_7 (not_7_out, Opcode[1]);
  not not_8 (not_8_out, Opcode[0]);
  and and_1 (out_3, Opcode[2], Opcode[1], Opcode[0]);
  and and_2 (out_4, Opcode[2], Opcode[1], not_9_out);
  not not_9 (not_9_out, Opcode[0]);
  and and_3 (out_5, not_1_out[2], not_1_out[1], not_1_out[0], Funct[3], Funct[2], not_10_out, Funct[0]);
  not not_10 (not_10_out, Funct[1]);
  and and_4 (and_4_out, not_2_out, not_3_out, not_4_out);
  xor xor_1 (xor_1_out, Funct[1], Funct[0]);
  not not_11 (not_11_out, Funct[2]);
  not not_12 (not_12_out, Funct[1]);
  not not_13 (not_13_out, Funct[0]);
  and and_5 (and_5_out, not_6_out, not_7_out, not_8_out);
  not not_14 (not_14_out, Funct[2]);
  not not_15 (not_15_out, Funct[0]);
  and and_6 (out_7[0], Opcode[2], Opcode[1], Opcode[0]);
  and and_7 (out_8, Opcode[2], Opcode[1], Opcode[0]);
  not not_16 (not_16_out, Opcode[2]);
  not not_17 (not_17_out, Opcode[0]);
  not not_18 (not_18_out, Opcode[1]);
  not not_19 (not_19_out, Opcode[1]);
  not not_20 (not_20_out, Opcode[0]);
  not not_21 (not_21_out, Opcode[2]);
  not not_22 (not_22_out, Opcode[1]);
  and and_8 (and_8_out, Funct[3], not_5_out, xor_1_out);
  and and_9 (out_6[0], and_4_out, Funct[3], not_11_out, not_12_out, not_13_out);
  and and_10 (out_7[1], and_5_out, Funct[3], not_14_out, not_15_out);
  not not_23 (not_23_out, Opcode[2]);
  xor xor_2 (xor_2_out, Opcode[1], Opcode[0]);
  and and_11 (and_11_out, Opcode[1], Opcode[0]);
  and and_12 (out_11, not_16_out, Opcode[1], not_17_out);
  and and_13 (out_12, Opcode[2], not_18_out, Opcode[0]);
  and and_14 (out_13, Opcode[2], not_19_out, not_20_out);
  and and_15 (out_14, not_21_out, not_22_out, Opcode[0]);
  and and_16 (out_6[1], and_4_out, and_8_out);
  not not_24 (not_24_out, Opcode[2]);
  not not_25 (not_25_out, Opcode[1]);
  not not_26 (not_26_out, Opcode[0]);
  not not_27 (not_27_out, Funct[1]);
  not not_28 (not_28_out, Opcode[2]);
  not not_29 (not_29_out, Opcode[1]);
  not not_30 (not_30_out, Opcode[1]);
  not not_31 (not_31_out, Opcode[0]);
  and and_17 (and_17_out, not_23_out, xor_2_out);
  and and_18 (and_18_out, xor_2_out, Opcode[2]);
  xor xor_3 (xor_3_out, Opcode[2], and_11_out);
  and and_19 (and_19_out, not_24_out, not_25_out, not_26_out, Funct[3], Funct[2], not_27_out, Funct[0]);
  and and_20 (and_20_out, not_28_out, not_29_out, Opcode[0]);
  and and_21 (and_21_out, Opcode[2], not_30_out, Opcode[0]);
  and and_22 (and_22_out, Opcode[2], Opcode[1], not_31_out);
  and and_23 (and_23_out, Opcode[2], Opcode[1], Opcode[0]);
  or or_1 (out_10, and_17_out, and_18_out, xor_3_out);
  or or_2 (or_2_out, and_19_out, and_20_out, and_21_out, and_22_out, and_23_out);
  not not_32 (out_9, or_2_out);

  // Notes on the sheet:
  //   CONTROL
  //   Branch
  //   Jump
  //   JR $RX
  //   RB
  //   RA
  //   RegDest
  //   RegWrite
  //   ALU A Src
  //   Alu B Src
  //   MemWrite
  //   MemToReg
  //   Disp
endmodule

module ZeroExtend4to8 (
  input  [3:0] in_1,
  output [7:0] out_2
);


  assign out_2 = {4'b0000, in_1};
endmodule

module jump (
  input  [4:0] Address,
  input  [7:0] in_2,
  output [7:0] New_PC
);


  assign New_PC = {in_2[7:5], Address};

  // Notes on the sheet:
  //   Current PC
endmodule

module Display (
  input  Clear,
  input  [7:0] Display_Value,
  input  [7:0] Imm,
  input  Display,
  output [7:0] out_5,
  output [7:0] out_6,
  output [7:0] out_7,
  output [7:0] out_8
);

  wire [7:0] demultiplexer_1_out0, demultiplexer_1_out1, demultiplexer_1_out2, demultiplexer_1_out3;

  Demultiplexer #(.select(2), .width(8), .tristate("true")) demultiplexer_1 (
    .out0(demultiplexer_1_out0), .out1(demultiplexer_1_out1), .out2(demultiplexer_1_out2),
    .out3(demultiplexer_1_out3), .in(Display_Value), .sel(Imm[1:0]));
  Register #(.width(8)) register_1 (.D(demultiplexer_1_out0), .Q(out_8), .clk(Display), .clr(Clear));  // open: en
  Register #(.width(8)) register_2 (.D(demultiplexer_1_out1), .Q(out_7), .clk(Display), .clr(Clear));  // open: en
  Register #(.width(8)) register_3 (.D(demultiplexer_1_out2), .Q(out_6), .clk(Display), .clr(Clear));  // open: en
  Register #(.width(8)) register_4 (.D(demultiplexer_1_out3), .Q(out_5), .clk(Display), .clr(Clear));  // open: en
endmodule

module branch (
  input  [4:0] Address,
  output [7:0] New_PC
);


  assign New_PC = {{4{Address[4]}}, Address[3:0]};
endmodule

module ControlALU (
  input  [2:0] Opcode,
  input  [3:0] Funct,
  output [3:0] out_3
);

  Multiplexer #(.select(3), .width(4)) multiplexer_1 (
    .in0(Funct), .in1(4'b1000), .in2(4'b0100), .in3(4'b0010), .in4(4'b0000), .in5(4'b0000), .in6(4'b0000),
    .in7(4'b0001), .out(out_3), .sel(Opcode));

  // Notes on the sheet:
  //   sll
  //   Move
  //   or
  //   add
  //   sub
  //   ALU Control
endmodule
